// Logisim project LC-3 ALU.circ as structural Verilog: 1 circuit, main circuit ALU
module ALU (
  input  [15:0] A,
  input  [15:0] B,
  input  [15:0] Rn,
  input  [3:0] ALUCtrl,
  output [15:0] ALUOutput,
  output [2:0] ALUFlags
);

  wire clock_1_out;
  wire [1:0] nor_2_out;
  wire [15:0] adder_1_out, and_1_out, multiplexer_2_out, not_1_out;

  Adder #(.width(16)) adder_1 (.a(A), .b(B), .out(adder_1_out));  // open: cin, cout
  assign and_1_out = A & B;  // AND_Gate and_1, 16 bits wide
  assign not_1_out = ~A;  // NOT_Gate not_1, 16 bits wide
  Multiplexer #(.select(2), .width(16)) multiplexer_1 (
    .in0(adder_1_out), .in1(and_1_out), .in2(not_1_out), .out(ALUOutput), .sel(ALUCtrl[1:0]));  // open: in3
  Multiplexer #(.width(16)) multiplexer_2 (.in0(ALUOutput), .in1(Rn), .out(multiplexer_2_out), .sel(ALUCtrl[2]));
  nor nor_1 (nor_2_out[1], multiplexer_2_out[7], multiplexer_2_out[0], multiplexer_2_out[1], multiplexer_2_out[2], multiplexer_2_out[3], multiplexer_2_out[4], multiplexer_2_out[5], multiplexer_2_out[6], multiplexer_2_out[8], multiplexer_2_out[9], multiplexer_2_out[10], multiplexer_2_out[11], multiplexer_2_out[12], multiplexer_2_out[13], multiplexer_2_out[14], multiplexer_2_out[15]);
  nor nor_2 (nor_2_out[0], nor_2_out[1], multiplexer_2_out[15]);
  Register #(.trigger("falling"), .width(3)) register_1 (
    .D({multiplexer_2_out[15], nor_2_out}), .en(ALUCtrl[3]), .clk(clock_1_out), .Q(ALUFlags));  // open: clr
  Clock clock_1 (.out(clock_1_out));
endmodule
