// Logisim project LC-3 BANCO.circ as structural Verilog: 1 circuit, main circuit BancoDeRegistros
module BancoDeRegistros (
  input  CLK,
  input  [2:0] A1,
  input  [2:0] A2,
  input  WE,
  input  [2:0] A3,
  input  [15:0] WD3,
  output [15:0] RD1,
  output [15:0] RD2
);

  wire decoder_1_out0, decoder_1_out1, decoder_1_out2, decoder_1_out3, decoder_1_out4, decoder_1_out5,
       decoder_1_out6, decoder_1_out7, not_1_out;
  wire [15:0] register_1_q, register_2_q, register_3_q, register_4_q, register_5_q, register_6_q,
       register_7_q, register_8_q;

  Decoder #(.select(3)) decoder_1 (
    .out0(decoder_1_out0), .out1(decoder_1_out1), .out2(decoder_1_out2), .out3(decoder_1_out3),
    .out4(decoder_1_out4), .out5(decoder_1_out5), .out6(decoder_1_out6), .out7(decoder_1_out7), .sel(A3),
    .en(WE));
  not not_1 (not_1_out, CLK);
  Register #(.width(16)) register_1 (.D(WD3), .en(decoder_1_out0), .clk(not_1_out), .Q(register_1_q));  // open: clr
  Register #(.width(16)) register_2 (.D(WD3), .en(decoder_1_out1), .clk(not_1_out), .Q(register_2_q));  // open: clr
  Register #(.width(16)) register_3 (.D(WD3), .en(decoder_1_out2), .clk(not_1_out), .Q(register_3_q));  // open: clr
  Register #(.width(16)) register_4 (.D(WD3), .en(decoder_1_out3), .clk(not_1_out), .Q(register_4_q));  // open: clr
  Register #(.width(16)) register_5 (.D(WD3), .en(decoder_1_out4), .clk(not_1_out), .Q(register_5_q));  // open: clr
  Register #(.width(16)) register_6 (.D(WD3), .en(decoder_1_out5), .clk(not_1_out), .Q(register_6_q));  // open: clr
  Register #(.width(16)) register_7 (.D(WD3), .en(decoder_1_out6), .clk(not_1_out), .Q(register_7_q));  // open: clr
  Register #(.width(16)) register_8 (.D(WD3), .en(decoder_1_out7), .clk(not_1_out), .Q(register_8_q));  // open: clr
  Multiplexer #(.select(3), .width(16)) multiplexer_1 (
    .in0(register_1_q), .in1(register_2_q), .in2(register_3_q), .in3(register_4_q), .in4(register_5_q),
    .in5(register_6_q), .in6(register_7_q), .in7(register_8_q), .out(RD1), .sel(A1));
  Multiplexer #(.select(3), .width(16)) multiplexer_2 (
    .in0(register_1_q), .in1(register_2_q), .in2(register_3_q), .in3(register_4_q), .in4(register_5_q),
    .in5(register_6_q), .in6(register_7_q), .in7(register_8_q), .out(RD2), .sel(A2));
endmodule
