// Logisim project LC-3 UNIDAD DE CONTROL.circ as structural Verilog: 2 circuits, main circuit UnidadDeControl
module UnidadDeControl (
  input  [3:0] OPCODE,
  input  Bit5,
  output SALTO_Cond,
  output SALTO_Incond,
  output WE_DM,
  output WE_RF,
  output [1:0] MUX_WB,
  output [1:0] MUX_EXT,
  output MUX_RD1,
  output MUX_A2_RF,
  output MUX_RD2,
  output [3:0] ALU_CTRL
);

  wire decodificadoropcode_1_mux_bit5;

  DecodificadorOpcode decodificadoropcode_1 (
    .OPCODE(OPCODE), .SALTO_Cond(SALTO_Cond), .SALTO_Incond(SALTO_Incond), .WE_DM(WE_DM), .WE_RF(WE_RF),
    .MUX_WB(MUX_WB), .MUX_EXT(MUX_EXT), .MUX_RD1(MUX_RD1), .MUX_A2_RF(MUX_A2_RF),
    .MUX_bit5(decodificadoropcode_1_mux_bit5), .ALU_CTRL(ALU_CTRL));
  Multiplexer multiplexer_1 (.in0(1'b1), .in1(Bit5), .out(MUX_RD2), .sel(decodificadoropcode_1_mux_bit5));
endmodule

module DecodificadorOpcode (
  input  [3:0] OPCODE,
  output SALTO_Cond,
  output SALTO_Incond,
  output WE_DM,
  output WE_RF,
  output [1:0] MUX_WB,
  output [1:0] MUX_EXT,
  output MUX_RD1,
  output MUX_A2_RF,
  output MUX_bit5,
  output [3:0] ALU_CTRL
);

  wire and_3_out, and_4_out, and_5_out, and_6_out, and_7_out, and_8_out, and_10_out, and_11_out, and_12_out,
       and_13_out, and_14_out, and_15_out, and_16_out, and_17_out, and_18_out, and_19_out, and_20_out,
       and_21_out, and_23_out, and_24_out, and_25_out, and_26_out, and_27_out, and_28_out, and_29_out,
       and_31_out, and_32_out, not_1_out, not_2_out, not_4_out;

  not not_1 (not_1_out, OPCODE[3]);
  not not_2 (not_2_out, OPCODE[2]);
  not not_3 (MUX_WB[1], OPCODE[1]);
  not not_4 (not_4_out, OPCODE[0]);
  and and_1 (SALTO_Cond, not_1_out, not_2_out, MUX_WB[1], not_4_out);
  and and_2 (SALTO_Incond, OPCODE[3], OPCODE[2], MUX_WB[1], not_4_out);
  and and_3 (and_3_out, not_1_out, OPCODE[1], OPCODE[0]);
  and and_4 (and_4_out, not_2_out, OPCODE[1], OPCODE[0]);
  and and_5 (and_5_out, not_1_out, MUX_WB[1], OPCODE[0]);
  and and_6 (and_6_out, not_1_out, OPCODE[1], not_4_out);
  and and_7 (and_7_out, not_2_out, MUX_WB[1], OPCODE[0]);
  and and_8 (and_8_out, not_2_out, OPCODE[1], not_4_out);
  and and_9 (MUX_WB[0], OPCODE[3], not_4_out);
  and and_10 (and_10_out, OPCODE[2], OPCODE[1]);
  and and_11 (and_11_out, OPCODE[3], OPCODE[2], not_4_out);
  and and_12 (and_12_out, not_1_out, not_2_out, not_4_out);
  and and_13 (and_13_out, not_2_out, OPCODE[1]);
  and and_14 (and_14_out, not_2_out, OPCODE[1]);
  and and_15 (and_15_out, not_1_out, MUX_WB[1], not_4_out);
  and and_16 (and_16_out, not_2_out, not_4_out);
  and and_17 (and_17_out, OPCODE[3], OPCODE[1], not_4_out);
  and and_18 (and_18_out, not_1_out, not_2_out, MUX_WB[1], not_4_out);
  and and_19 (and_19_out, OPCODE[1], OPCODE[0]);
  and and_20 (and_20_out, not_1_out, OPCODE[2], OPCODE[1]);
  and and_21 (and_21_out, OPCODE[3], OPCODE[2], MUX_WB[1], not_4_out);
  and and_22 (MUX_bit5, not_1_out, MUX_WB[1], OPCODE[0]);
  and and_23 (and_23_out, OPCODE[1], not_4_out);
  and and_24 (and_24_out, not_1_out, OPCODE[2], MUX_WB[1]);
  and and_25 (and_25_out, OPCODE[3], not_2_out, MUX_WB[1]);
  and and_26 (and_26_out, not_1_out, MUX_WB[1], OPCODE[0]);
  and and_27 (and_27_out, OPCODE[1], not_4_out);
  and and_28 (and_28_out, not_1_out, OPCODE[2], not_4_out);
  and and_29 (and_29_out, OPCODE[3], not_2_out, not_4_out);
  and and_30 (ALU_CTRL[1], OPCODE[3], not_2_out, MUX_WB[1], OPCODE[0]);
  and and_31 (and_31_out, not_1_out, OPCODE[2], MUX_WB[1]);
  and and_32 (and_32_out, OPCODE[3], not_2_out, MUX_WB[1], not_4_out);
  or or_1 (WE_DM, and_3_out, and_4_out);
  or or_2 (WE_RF, and_5_out, and_6_out, and_7_out, and_8_out);
  or or_3 (MUX_EXT[1], and_10_out, and_11_out);
  or or_4 (MUX_EXT[0], and_12_out, and_13_out);
  or or_5 (MUX_RD1, and_14_out, and_15_out, and_16_out, and_17_out);
  or or_6 (MUX_A2_RF, and_18_out, and_19_out, and_20_out, and_21_out);
  or or_7 (ALU_CTRL[3], and_23_out, and_24_out, and_25_out, and_26_out);
  or or_8 (ALU_CTRL[2], and_27_out, and_28_out, and_29_out);
  or or_9 (ALU_CTRL[0], and_31_out, and_32_out);
endmodule
