// Logisim project Pipelined_Processor.circ as structural Verilog: 14 circuits, main circuit test
module test (
  input  [3:0] in_1
);

  wire CLK, decoopcode_1_a1, decoopcode_1_a2, decoopcode_1_a3, decoopcode_1_b1, decoopcode_1_b2,
       decoopcode_1_b3, decoopcode_1_c1, decoopcode_1_c2, decoopcode_1_c3, decoopcode_1_d1, decoopcode_1_d2,
       decoopcode_1_d3, decoopcode_1_e1, decoopcode_1_e2, decoopcode_1_e3, decoopcode_1_f1, decoopcode_1_f2,
       decoopcode_1_f3, decoopcode_1_g1, decoopcode_1_g2, decoopcode_1_g3, decoopcode_1_p1, decoopcode_1_p2,
       decoopcode_1_p3, decoopcode_2_a1, decoopcode_2_a2, decoopcode_2_a3, decoopcode_2_b1, decoopcode_2_b2,
       decoopcode_2_b3, decoopcode_2_c1, decoopcode_2_c2, decoopcode_2_c3, decoopcode_2_d1, decoopcode_2_d2,
       decoopcode_2_d3, decoopcode_2_e1, decoopcode_2_e2, decoopcode_2_e3, decoopcode_2_f1, decoopcode_2_f2,
       decoopcode_2_f3, decoopcode_2_g1, decoopcode_2_g2, decoopcode_2_g3, decoopcode_2_p1, decoopcode_2_p2,
       decoopcode_2_p3, decoopcode_3_a1, decoopcode_3_a2, decoopcode_3_a3, decoopcode_3_b1, decoopcode_3_b2,
       decoopcode_3_b3, decoopcode_3_c1, decoopcode_3_c2, decoopcode_3_c3, decoopcode_3_d1, decoopcode_3_d2,
       decoopcode_3_d3, decoopcode_3_e1, decoopcode_3_e2, decoopcode_3_e3, decoopcode_3_f1, decoopcode_3_f2,
       decoopcode_3_f3, decoopcode_3_g1, decoopcode_3_g2, decoopcode_3_g3, decoopcode_3_p1, decoopcode_3_p2,
       decoopcode_3_p3, decoopcode_4_a1, decoopcode_4_a2, decoopcode_4_a3, decoopcode_4_b1, decoopcode_4_b2,
       decoopcode_4_b3, decoopcode_4_c1, decoopcode_4_c2, decoopcode_4_c3, decoopcode_4_d1, decoopcode_4_d2,
       decoopcode_4_d3, decoopcode_4_e1, decoopcode_4_e2, decoopcode_4_e3, decoopcode_4_f1, decoopcode_4_f2,
       decoopcode_4_f3, decoopcode_4_g1, decoopcode_4_g2, decoopcode_4_g3, decoopcode_4_p1, decoopcode_4_p2,
       decoopcode_4_p3, decoopcode_5_a1, decoopcode_5_a2, decoopcode_5_a3, decoopcode_5_b1, decoopcode_5_b2,
       decoopcode_5_b3, decoopcode_5_c1, decoopcode_5_c2, decoopcode_5_c3, decoopcode_5_d1, decoopcode_5_d2,
       decoopcode_5_d3, decoopcode_5_e1, decoopcode_5_e2, decoopcode_5_e3, decoopcode_5_f1, decoopcode_5_f2,
       decoopcode_5_f3, decoopcode_5_g1, decoopcode_5_g2, decoopcode_5_g3, decoopcode_5_p1, decoopcode_5_p2,
       decoopcode_5_p3, decoopcode_6_a1, decoopcode_6_a2, decoopcode_6_a3, decoopcode_6_b1, decoopcode_6_b2,
       decoopcode_6_b3, decoopcode_6_c1, decoopcode_6_c2, decoopcode_6_c3, decoopcode_6_d1, decoopcode_6_d2,
       decoopcode_6_d3, decoopcode_6_e1, decoopcode_6_e2, decoopcode_6_e3, decoopcode_6_f1, decoopcode_6_f2,
       decoopcode_6_f3, decoopcode_6_g1, decoopcode_6_g2, decoopcode_6_g3, decoopcode_6_p1, decoopcode_6_p2,
       decoopcode_6_p3, executeregister_1_rd1_pc1_ex, executeregister_1_rd2_exts_ex,
       executeregister_1_saltocon_ex, executeregister_1_saltoinc_ex, executeregister_1_wem_ex,
       executeregister_1_wer_ex, logicanzp_1_salida, memoryregister_1_salto_conm,
       memoryregister_1_salto_incm, memoryregister_1_wem_m, memoryregister_1_wer_m, MUX_PC, or_1_out,
       unidaddecontrol_1_mux_a2_rf, unidaddecontrol_1_mux_rd1, unidaddecontrol_1_mux_rd2,
       unidaddecontrol_1_salto_cond, unidaddecontrol_1_salto_incond, unidaddecontrol_1_we_dm,
       unidaddecontrol_1_we_rf, wb_register_1_wer_wb;
  wire [1:0] executeregister_1_mux_wbex, memoryregister_1_mux_wb_m, unidaddecontrol_1_mux_ext,
       unidaddecontrol_1_mux_wb, wb_register_1_mux_wb;
  wire [2:0] alu_1_aluflags, executeregister_1_nzp_ex, executeregister_1_wa3ex, memoryregister_1_alufm,
       memoryregister_1_nzpm, memoryregister_1_wa3_m, multiplexer_2_out, undriven;
  wire [3:0] executeregister_1_alucontrolex, executeregister_1_opcode_ex, memoryregister_1_opcode_m,
       unidaddecontrol_1_alu_ctrl, wb_register_1_opcode_w;
  wire [15:0] adder_1_out, alu_1_aluoutput, bancoderegistros_1_rd1, bancoderegistros_1_rd2, datamemory_1_rd1,
       decoderegister_1_insd, decoderegister_1_pc1d, executeregister_1_extsex, executeregister_1_pcplus1ex,
       executeregister_1_rd1ex, executeregister_1_rd2ex, extensorsigno_1_exts, instructionmemory_1_rd,
       memoryregister_1_aluresultm, memoryregister_1_pcplusm, memoryregister_1_rd2m, multiplexer_1_out,
       multiplexer_3_out, multiplexer_4_out, multiplexer_5_out, register_1_q, wb_register_1_aluresult_w,
       wb_register_1_pcplus_w, wb_register_1_rd_w;

  Clock clock_1 (.out(CLK));
  _7_Segment_Display u_7_segment_display_1 (
    .g(decoopcode_1_a1), .f(decoopcode_1_b1), .a(decoopcode_1_c1), .b(decoopcode_1_d1), .e(decoopcode_1_e1),
    .d(decoopcode_1_g1), .c(decoopcode_1_f1), .dp(decoopcode_1_p1));
  DecoOPCODE decoopcode_1 (
    .OPCODE(in_1), .A2(decoopcode_1_a2), .A3(decoopcode_1_a3), .B1(decoopcode_1_b1), .B2(decoopcode_1_b2),
    .B3(decoopcode_1_b3), .C1(decoopcode_1_c1), .C2(decoopcode_1_c2), .C3(decoopcode_1_c3),
    .D1(decoopcode_1_d1), .D2(decoopcode_1_d2), .D3(decoopcode_1_d3), .E1(decoopcode_1_e1),
    .E2(decoopcode_1_e2), .E3(decoopcode_1_e3), .F1(decoopcode_1_f1), .F2(decoopcode_1_f2),
    .F3(decoopcode_1_f3), .G1(decoopcode_1_g1), .G2(decoopcode_1_g2), .G3(decoopcode_1_g3),
    .P1(decoopcode_1_p1), .P2(decoopcode_1_p2), .P3(decoopcode_1_p3), .A1(decoopcode_1_a1));
  Register #(.width(16)) register_1 (.D(multiplexer_1_out), .clk(CLK), .Q(register_1_q));  // open: en, clr
  Multiplexer #(.width(16)) multiplexer_1 (
    .in0(adder_1_out), .in1(multiplexer_5_out), .out(multiplexer_1_out), .sel(MUX_PC));
  _7_Segment_Display u_7_segment_display_2 (
    .g(decoopcode_1_a2), .f(decoopcode_1_b2), .a(decoopcode_1_c2), .b(decoopcode_1_d2), .e(decoopcode_1_e2),
    .d(decoopcode_1_g2), .c(decoopcode_1_f2), .dp(decoopcode_1_p2));
  _7_Segment_Display u_7_segment_display_3 (
    .g(decoopcode_1_a3), .f(decoopcode_1_b3), .a(decoopcode_1_c3), .b(decoopcode_1_d3), .e(decoopcode_1_e3),
    .d(decoopcode_1_g3), .c(decoopcode_1_f3), .dp(decoopcode_1_p3));
  DecoOPCODE decoopcode_2 (
    .OPCODE(instructionmemory_1_rd[15:12]), .A2(decoopcode_2_a2), .A3(decoopcode_2_a3), .B1(decoopcode_2_b1),
    .B2(decoopcode_2_b2), .B3(decoopcode_2_b3), .C1(decoopcode_2_c1), .C2(decoopcode_2_c2),
    .C3(decoopcode_2_c3), .D1(decoopcode_2_d1), .D2(decoopcode_2_d2), .D3(decoopcode_2_d3),
    .E1(decoopcode_2_e1), .E2(decoopcode_2_e2), .E3(decoopcode_2_e3), .F1(decoopcode_2_f1),
    .F2(decoopcode_2_f2), .F3(decoopcode_2_f3), .G1(decoopcode_2_g1), .G2(decoopcode_2_g2),
    .G3(decoopcode_2_g3), .P1(decoopcode_2_p1), .P2(decoopcode_2_p2), .P3(decoopcode_2_p3),
    .A1(decoopcode_2_a1));
  _7_Segment_Display u_7_segment_display_4 (
    .g(decoopcode_2_a1), .f(decoopcode_2_b1), .a(decoopcode_2_c1), .b(decoopcode_2_d1), .e(decoopcode_2_e1),
    .d(decoopcode_2_g1), .c(decoopcode_2_f1), .dp(decoopcode_2_p1));
  _7_Segment_Display u_7_segment_display_5 (
    .g(decoopcode_2_a2), .f(decoopcode_2_b2), .a(decoopcode_2_c2), .b(decoopcode_2_d2), .e(decoopcode_2_e2),
    .d(decoopcode_2_g2), .c(decoopcode_2_f2), .dp(decoopcode_2_p2));
  InstructionMemory instructionmemory_1 (.A(register_1_q), .RD(instructionmemory_1_rd));
  Adder #(.width(16)) adder_1 (.a(register_1_q), .b(16'h1), .out(adder_1_out));  // open: cin, cout
  _7_Segment_Display u_7_segment_display_6 (
    .g(decoopcode_2_a3), .f(decoopcode_2_b3), .a(decoopcode_2_c3), .b(decoopcode_2_d3), .e(decoopcode_2_e3),
    .d(decoopcode_2_g3), .c(decoopcode_2_f3), .dp(decoopcode_2_p3));
  DecodeRegister decoderegister_1 (
    .CLK(CLK), .PC1F(adder_1_out), .InsF(instructionmemory_1_rd), .InsD(decoderegister_1_insd),
    .PC1D(decoderegister_1_pc1d));  // open: CLR, WE
  _7_Segment_Display u_7_segment_display_7 (
    .g(decoopcode_3_a1), .f(decoopcode_3_b1), .a(decoopcode_3_c1), .b(decoopcode_3_d1), .e(decoopcode_3_e1),
    .d(decoopcode_3_g1), .c(decoopcode_3_f1), .dp(decoopcode_3_p1));
  DecoOPCODE decoopcode_3 (
    .OPCODE(decoderegister_1_insd[15:12]), .A2(decoopcode_3_a2), .A3(decoopcode_3_a3), .B1(decoopcode_3_b1),
    .B2(decoopcode_3_b2), .B3(decoopcode_3_b3), .C1(decoopcode_3_c1), .C2(decoopcode_3_c2),
    .C3(decoopcode_3_c3), .D1(decoopcode_3_d1), .D2(decoopcode_3_d2), .D3(decoopcode_3_d3),
    .E1(decoopcode_3_e1), .E2(decoopcode_3_e2), .E3(decoopcode_3_e3), .F1(decoopcode_3_f1),
    .F2(decoopcode_3_f2), .F3(decoopcode_3_f3), .G1(decoopcode_3_g1), .G2(decoopcode_3_g2),
    .G3(decoopcode_3_g3), .P1(decoopcode_3_p1), .P2(decoopcode_3_p2), .P3(decoopcode_3_p3),
    .A1(decoopcode_3_a1));
  _7_Segment_Display u_7_segment_display_8 (
    .g(decoopcode_3_a2), .f(decoopcode_3_b2), .a(decoopcode_3_c2), .b(decoopcode_3_d2), .e(decoopcode_3_e2),
    .d(decoopcode_3_g2), .c(decoopcode_3_f2), .dp(decoopcode_3_p2));
  _7_Segment_Display u_7_segment_display_9 (
    .g(decoopcode_3_a3), .f(decoopcode_3_b3), .a(decoopcode_3_c3), .b(decoopcode_3_d3), .e(decoopcode_3_e3),
    .d(decoopcode_3_g3), .c(decoopcode_3_f3), .dp(decoopcode_3_p3));
  UnidadDeControl unidaddecontrol_1 (
    .OPCODE(decoderegister_1_insd[15:12]), .Bit5(decoderegister_1_insd[5]),
    .SALTO_Cond(unidaddecontrol_1_salto_cond), .SALTO_Incond(unidaddecontrol_1_salto_incond),
    .WE_DM(unidaddecontrol_1_we_dm), .WE_RF(unidaddecontrol_1_we_rf), .MUX_WB(unidaddecontrol_1_mux_wb),
    .MUX_EXT(unidaddecontrol_1_mux_ext), .MUX_RD1(unidaddecontrol_1_mux_rd1),
    .MUX_A2_RF(unidaddecontrol_1_mux_a2_rf), .MUX_RD2(unidaddecontrol_1_mux_rd2),
    .ALU_CTRL(unidaddecontrol_1_alu_ctrl));
  Multiplexer #(.width(3)) multiplexer_2 (
    .in0(decoderegister_1_insd[2:0]), .in1(decoderegister_1_insd[11:9]), .out(multiplexer_2_out),
    .sel(unidaddecontrol_1_mux_a2_rf));
  BancoDeRegistros bancoderegistros_1 (
    .A3(undriven), .WD3(multiplexer_5_out), .CLK(CLK), .WE(wb_register_1_wer_wb),
    .A1(decoderegister_1_insd[8:6]), .A2(multiplexer_2_out), .RD1(bancoderegistros_1_rd1),
    .RD2(bancoderegistros_1_rd2));
  ExtensorSigno extensorsigno_1 (
    .bit10a0(decoderegister_1_insd[10:0]), .Ext_S(unidaddecontrol_1_mux_ext), .ExtS(extensorsigno_1_exts));
  _7_Segment_Display u_7_segment_display_10 (
    .g(decoopcode_4_a1), .f(decoopcode_4_b1), .a(decoopcode_4_c1), .b(decoopcode_4_d1), .e(decoopcode_4_e1),
    .d(decoopcode_4_g1), .c(decoopcode_4_f1), .dp(decoopcode_4_p1));
  _7_Segment_Display u_7_segment_display_11 (
    .g(decoopcode_4_a2), .f(decoopcode_4_b2), .a(decoopcode_4_c2), .b(decoopcode_4_d2), .e(decoopcode_4_e2),
    .d(decoopcode_4_g2), .c(decoopcode_4_f2), .dp(decoopcode_4_p2));
  DecoOPCODE decoopcode_4 (
    .OPCODE(executeregister_1_opcode_ex), .A2(decoopcode_4_a2), .A3(decoopcode_4_a3), .B1(decoopcode_4_b1),
    .B2(decoopcode_4_b2), .B3(decoopcode_4_b3), .C1(decoopcode_4_c1), .C2(decoopcode_4_c2),
    .C3(decoopcode_4_c3), .D1(decoopcode_4_d1), .D2(decoopcode_4_d2), .D3(decoopcode_4_d3),
    .E1(decoopcode_4_e1), .E2(decoopcode_4_e2), .E3(decoopcode_4_e3), .F1(decoopcode_4_f1),
    .F2(decoopcode_4_f2), .F3(decoopcode_4_f3), .G1(decoopcode_4_g1), .G2(decoopcode_4_g2),
    .G3(decoopcode_4_g3), .P1(decoopcode_4_p1), .P2(decoopcode_4_p2), .P3(decoopcode_4_p3),
    .A1(decoopcode_4_a1));
  ExecuteRegister executeregister_1 (
    .WER(unidaddecontrol_1_we_rf), .WEM(unidaddecontrol_1_we_dm), .RD1_PC1(unidaddecontrol_1_mux_rd1),
    .SaltoINC(unidaddecontrol_1_salto_incond), .SaltoCON(unidaddecontrol_1_salto_cond),
    .RD2_ExtS(unidaddecontrol_1_mux_rd2), .RD1D(bancoderegistros_1_rd1), .RD2D(bancoderegistros_1_rd2),
    .PCPlus1D(decoderegister_1_pc1d), .ExtSD(extensorsigno_1_exts), .CLK(CLK),
    .OPCODE(decoderegister_1_insd[15:12]), .ALUControl(unidaddecontrol_1_alu_ctrl),
    .NZP_D(decoderegister_1_insd[11:9]), .WA3D(undriven), .MUX_WB(unidaddecontrol_1_mux_wb),
    .WER_Ex(executeregister_1_wer_ex), .WEM_Ex(executeregister_1_wem_ex),
    .RD1_PC1_Ex(executeregister_1_rd1_pc1_ex), .SaltoINC_Ex(executeregister_1_saltoinc_ex),
    .SaltoCON_Ex(executeregister_1_saltocon_ex), .RD2_ExtS_Ex(executeregister_1_rd2_exts_ex),
    .RD1Ex(executeregister_1_rd1ex), .RD2Ex(executeregister_1_rd2ex),
    .PCPlus1Ex(executeregister_1_pcplus1ex), .ExtSEx(executeregister_1_extsex),
    .OPCODE_Ex(executeregister_1_opcode_ex), .ALUControlEx(executeregister_1_alucontrolex),
    .NZP_Ex(executeregister_1_nzp_ex), .WA3Ex(executeregister_1_wa3ex), .MUX_WBEx(executeregister_1_mux_wbex));  // open: Ins, out_33
  _7_Segment_Display u_7_segment_display_12 (
    .g(decoopcode_4_a3), .f(decoopcode_4_b3), .a(decoopcode_4_c3), .b(decoopcode_4_d3), .e(decoopcode_4_e3),
    .d(decoopcode_4_g3), .c(decoopcode_4_f3), .dp(decoopcode_4_p3));
  Multiplexer #(.width(16)) multiplexer_3 (
    .in0(executeregister_1_rd1ex), .in1(executeregister_1_pcplus1ex), .out(multiplexer_3_out),
    .sel(executeregister_1_rd1_pc1_ex));
  Multiplexer #(.width(16)) multiplexer_4 (
    .in0(executeregister_1_rd2ex), .in1(executeregister_1_extsex), .out(multiplexer_4_out),
    .sel(executeregister_1_rd2_exts_ex));
  Hazard hazard_1 ();  // open: OP, bit5, DR, SR1, SR2, MUX_A_ALU, MUX_B_ALU
  _7_Segment_Display u_7_segment_display_13 (
    .g(decoopcode_5_a1), .f(decoopcode_5_b1), .a(decoopcode_5_c1), .b(decoopcode_5_d1), .e(decoopcode_5_e1),
    .d(decoopcode_5_g1), .c(decoopcode_5_f1), .dp(decoopcode_5_p1));
  DecoOPCODE decoopcode_5 (
    .OPCODE(memoryregister_1_opcode_m), .A2(decoopcode_5_a2), .A3(decoopcode_5_a3), .B1(decoopcode_5_b1),
    .B2(decoopcode_5_b2), .B3(decoopcode_5_b3), .C1(decoopcode_5_c1), .C2(decoopcode_5_c2),
    .C3(decoopcode_5_c3), .D1(decoopcode_5_d1), .D2(decoopcode_5_d2), .D3(decoopcode_5_d3),
    .E1(decoopcode_5_e1), .E2(decoopcode_5_e2), .E3(decoopcode_5_e3), .F1(decoopcode_5_f1),
    .F2(decoopcode_5_f2), .F3(decoopcode_5_f3), .G1(decoopcode_5_g1), .G2(decoopcode_5_g2),
    .G3(decoopcode_5_g3), .P1(decoopcode_5_p1), .P2(decoopcode_5_p2), .P3(decoopcode_5_p3),
    .A1(decoopcode_5_a1));
  ALU alu_1 (
    .A(multiplexer_3_out), .B(multiplexer_4_out), .ALUCtrl(executeregister_1_alucontrolex),
    .Rn(multiplexer_5_out), .ALUOutput(alu_1_aluoutput), .ALUFlags(alu_1_aluflags));
  MemoryRegister memoryregister_1 (
    .WEM_Ex(executeregister_1_wem_ex), .WER_Ex(executeregister_1_wer_ex),
    .Salto_IncEx(executeregister_1_saltoinc_ex), .Salto_ConEx(executeregister_1_saltocon_ex),
    .ALUResultEx(alu_1_aluoutput), .RD2Ex(executeregister_1_rd2ex), .PCPlusEx(executeregister_1_pcplus1ex),
    .CLK(CLK), .OPCODE_Ex(executeregister_1_opcode_ex), .WA3_Ex(executeregister_1_wa3ex),
    .MUX_WB_Ex(executeregister_1_mux_wbex), .NZPEx(executeregister_1_nzp_ex), .ALUFEx(alu_1_aluflags),
    .WEM_M(memoryregister_1_wem_m), .WER_M(memoryregister_1_wer_m), .ALUResultM(memoryregister_1_aluresultm),
    .RD2M(memoryregister_1_rd2m), .PCPlusM(memoryregister_1_pcplusm), .OPCODE_M(memoryregister_1_opcode_m),
    .Salto_IncM(memoryregister_1_salto_incm), .Salto_ConM(memoryregister_1_salto_conm),
    .WA3_M(memoryregister_1_wa3_m), .MUX_WB_M(memoryregister_1_mux_wb_m), .NZPM(memoryregister_1_nzpm),
    .ALUFM(memoryregister_1_alufm));
  _7_Segment_Display u_7_segment_display_14 (
    .g(decoopcode_5_a2), .f(decoopcode_5_b2), .a(decoopcode_5_c2), .b(decoopcode_5_d2), .e(decoopcode_5_e2),
    .d(decoopcode_5_g2), .c(decoopcode_5_f2), .dp(decoopcode_5_p2));
  _7_Segment_Display u_7_segment_display_15 (
    .g(decoopcode_5_a3), .f(decoopcode_5_b3), .a(decoopcode_5_c3), .b(decoopcode_5_d3), .e(decoopcode_5_e3),
    .d(decoopcode_5_g3), .c(decoopcode_5_f3), .dp(decoopcode_5_p3));
  LogicaNZP logicanzp_1 (
    .INS_NZP(memoryregister_1_nzpm), .ALU_NZP(memoryregister_1_alufm),
    .Salto_Cond(memoryregister_1_salto_conm), .Salida(logicanzp_1_salida));
  DataMemory datamemory_1 (
    .WE(memoryregister_1_wem_m), .CLK(CLK), .A1(memoryregister_1_aluresultm),
    .A2(memoryregister_1_aluresultm), .WD2(memoryregister_1_rd2m), .RD1(datamemory_1_rd1));
  or or_1 (or_1_out, memoryregister_1_salto_incm, logicanzp_1_salida);
  _7_Segment_Display u_7_segment_display_16 (
    .g(decoopcode_6_a1), .f(decoopcode_6_b1), .a(decoopcode_6_c1), .b(decoopcode_6_d1), .e(decoopcode_6_e1),
    .d(decoopcode_6_g1), .c(decoopcode_6_f1), .dp(decoopcode_6_p1));
  _7_Segment_Display u_7_segment_display_17 (
    .g(decoopcode_6_a2), .f(decoopcode_6_b2), .a(decoopcode_6_c2), .b(decoopcode_6_d2), .e(decoopcode_6_e2),
    .d(decoopcode_6_g2), .c(decoopcode_6_f2), .dp(decoopcode_6_p2));
  DecoOPCODE decoopcode_6 (
    .OPCODE(wb_register_1_opcode_w), .A2(decoopcode_6_a2), .A3(decoopcode_6_a3), .B1(decoopcode_6_b1),
    .B2(decoopcode_6_b2), .B3(decoopcode_6_b3), .C1(decoopcode_6_c1), .C2(decoopcode_6_c2),
    .C3(decoopcode_6_c3), .D1(decoopcode_6_d1), .D2(decoopcode_6_d2), .D3(decoopcode_6_d3),
    .E1(decoopcode_6_e1), .E2(decoopcode_6_e2), .E3(decoopcode_6_e3), .F1(decoopcode_6_f1),
    .F2(decoopcode_6_f2), .F3(decoopcode_6_f3), .G1(decoopcode_6_g1), .G2(decoopcode_6_g2),
    .G3(decoopcode_6_g3), .P1(decoopcode_6_p1), .P2(decoopcode_6_p2), .P3(decoopcode_6_p3),
    .A1(decoopcode_6_a1));
  WB_Register wb_register_1 (
    .ALUResult_M(memoryregister_1_aluresultm), .PCPlus_M(memoryregister_1_pcplusm),
    .OPCODE_M(memoryregister_1_opcode_m), .CLK(CLK), .MUX_PC_M(or_1_out), .RD_M(datamemory_1_rd1),
    .WA3_M(memoryregister_1_wa3_m), .MUX_WB_M(memoryregister_1_mux_wb_m), .WER_M(memoryregister_1_wer_m),
    .ALUResult_W(wb_register_1_aluresult_w), .PCPlus_W(wb_register_1_pcplus_w),
    .OPCODE_W(wb_register_1_opcode_w), .MUX_PC_WB(MUX_PC), .RD_W(wb_register_1_rd_w),
    .WA3_W(decoderegister_1_insd[11:9]), .MUX_WB(wb_register_1_mux_wb), .WER_WB(wb_register_1_wer_wb));
  _7_Segment_Display u_7_segment_display_18 (
    .g(decoopcode_6_a3), .f(decoopcode_6_b3), .a(decoopcode_6_c3), .b(decoopcode_6_d3), .e(decoopcode_6_e3),
    .d(decoopcode_6_g3), .c(decoopcode_6_f3), .dp(decoopcode_6_p3));
  Multiplexer #(.select(2), .width(16)) multiplexer_5 (
    .in0(wb_register_1_rd_w), .in2(wb_register_1_aluresult_w), .in3(wb_register_1_pcplus_w),
    .out(multiplexer_5_out), .sel(wb_register_1_mux_wb));  // open: in1
endmodule

module DecodeRegister (
  input  [15:0] InsF,
  input  CLK,
  input  CLR,
  input  [15:0] PC1F,
  input  WE,
  output [15:0] InsD,
  output [15:0] PC1D
);

  Register #(.width(16)) register_1 (.D(InsF), .en(WE), .clk(CLK), .Q(InsD), .clr(CLR));
  Register #(.width(16)) register_2 (.D(PC1F), .en(WE), .clk(CLK), .Q(PC1D), .clr(CLR));

  // Notes on the sheet:
  //   CLR: pull=down
  //   InsF: pull=up
  //   WE: pull=up
endmodule

module ExecuteRegister (
  input  [15:0] RD1D,
  input  [3:0] ALUControl,
  input  WER,
  input  [15:0] RD2D,
  input  [2:0] NZP_D,
  input  WEM,
  input  [15:0] PCPlus1D,
  input  [2:0] WA3D,
  input  RD1_PC1,
  input  [15:0] ExtSD,
  input  [1:0] MUX_WB,
  input  SaltoINC,
  input  CLK,
  input  SaltoCON,
  input  [3:0] OPCODE,
  input  RD2_ExtS,
  input  [15:0] Ins,
  output [15:0] RD1Ex,
  output [3:0] ALUControlEx,
  output WER_Ex,
  output [15:0] RD2Ex,
  output [2:0] NZP_Ex,
  output WEM_Ex,
  output [15:0] PCPlus1Ex,
  output [2:0] WA3Ex,
  output RD1_PC1_Ex,
  output [15:0] ExtSEx,
  output [1:0] MUX_WBEx,
  output SaltoINC_Ex,
  output SaltoCON_Ex,
  output [3:0] OPCODE_Ex,
  output RD2_ExtS_Ex,
  output [15:0] out_33
);

  Register #(.width(16)) register_1 (.D(RD1D), .en(1'b1), .clk(CLK), .Q(RD1Ex));  // open: clr
  Register #(.width(16)) register_2 (.D(RD2D), .en(1'b1), .clk(CLK), .Q(RD2Ex));  // open: clr
  Register #(.width(16)) register_3 (.D(PCPlus1D), .en(1'b1), .clk(CLK), .Q(PCPlus1Ex));  // open: clr
  Register #(.width(16)) register_4 (.D(ExtSD), .en(1'b1), .clk(CLK), .Q(ExtSEx));  // open: clr
  Register #(.width(4)) register_5 (.D(OPCODE), .en(1'b1), .clk(CLK), .Q(OPCODE_Ex));  // open: clr
  Register #(.width(4)) register_6 (.D(ALUControl), .en(1'b1), .clk(CLK), .Q(ALUControlEx));  // open: clr
  Register #(.width(3)) register_7 (.D(NZP_D), .en(1'b1), .clk(CLK), .Q(NZP_Ex));  // open: clr
  Register #(.width(3)) register_8 (.D(WA3D), .en(1'b1), .clk(CLK), .Q(WA3Ex));  // open: clr
  Register #(.width(2)) register_9 (.D(MUX_WB), .en(1'b1), .clk(CLK), .Q(MUX_WBEx));  // open: clr
  Register #(.width(1)) register_10 (.D(WER), .en(1'b1), .clk(CLK), .Q(WER_Ex));  // open: clr
  Register #(.width(1)) register_11 (.D(WEM), .en(1'b1), .clk(CLK), .Q(WEM_Ex));  // open: clr
  Register #(.width(1)) register_12 (.D(RD1_PC1), .en(1'b1), .clk(CLK), .Q(RD1_PC1_Ex));  // open: clr
  Register #(.width(1)) register_13 (.D(SaltoINC), .en(1'b1), .clk(CLK), .Q(SaltoINC_Ex));  // open: clr
  Register #(.width(1)) register_14 (.D(SaltoCON), .en(1'b1), .clk(CLK), .Q(SaltoCON_Ex));  // open: clr
  Register #(.width(1)) register_15 (.D(RD2_ExtS), .en(1'b1), .clk(CLK), .Q(RD2_ExtS_Ex));  // open: clr
  Register #(.width(16)) register_16 (.D(Ins), .en(1'b1), .clk(CLK), .Q(out_33));  // open: clr
endmodule

module ExtensorSigno (
  input  [10:0] bit10a0,
  input  [1:0] Ext_S,
  output [15:0] ExtS
);

  wire [15:0] bit_extender_1_out, bit_extender_2_out, bit_extender_3_out, bit_extender_4_out;

  assign bit_extender_1_out = {{11{bit10a0[4]}}, bit10a0[4:0]};  // Bit_Extender bit_extender_1
  assign bit_extender_2_out = {{10{bit10a0[5]}}, bit10a0[5:0]};  // Bit_Extender bit_extender_2
  assign bit_extender_3_out = {{7{bit10a0[8]}}, bit10a0[8:0]};  // Bit_Extender bit_extender_3
  assign bit_extender_4_out = {{5{bit10a0[10]}}, bit10a0};  // Bit_Extender bit_extender_4
  Multiplexer #(.select(2), .width(16)) multiplexer_1 (
    .in0(bit_extender_1_out), .in1(bit_extender_2_out), .in2(bit_extender_3_out), .in3(bit_extender_4_out),
    .out(ExtS), .sel(Ext_S));
endmodule

module MemoryRegister (
  input  [15:0] ALUResultEx,
  input  [15:0] RD2Ex,
  input  WEM_Ex,
  input  [15:0] PCPlusEx,
  input  [2:0] WA3_Ex,
  input  WER_Ex,
  input  CLK,
  input  [1:0] MUX_WB_Ex,
  input  [3:0] OPCODE_Ex,
  input  [2:0] NZPEx,
  input  Salto_IncEx,
  input  [2:0] ALUFEx,
  input  Salto_ConEx,
  output [15:0] ALUResultM,
  output [15:0] RD2M,
  output WEM_M,
  output [15:0] PCPlusM,
  output [2:0] WA3_M,
  output WER_M,
  output [1:0] MUX_WB_M,
  output [3:0] OPCODE_M,
  output [2:0] NZPM,
  output Salto_IncM,
  output [2:0] ALUFM,
  output Salto_ConM
);

  Register #(.width(16)) register_1 (.D(ALUResultEx), .en(1'b1), .clk(CLK), .Q(ALUResultM));  // open: clr
  Register #(.width(16)) register_2 (.D(RD2Ex), .en(1'b1), .clk(CLK), .Q(RD2M));  // open: clr
  Register #(.width(16)) register_3 (.D(PCPlusEx), .en(1'b1), .clk(CLK), .Q(PCPlusM));  // open: clr
  Register #(.width(4)) register_4 (.D(OPCODE_Ex), .en(1'b1), .clk(CLK), .Q(OPCODE_M));  // open: clr
  Register #(.width(1)) register_5 (.D(Salto_IncEx), .en(1'b1), .clk(CLK), .Q(Salto_IncM));  // open: clr
  Register #(.width(1)) register_6 (.D(Salto_ConEx), .en(1'b1), .clk(CLK), .Q(Salto_ConM));  // open: clr
  Register #(.width(3)) register_7 (.D(WA3_Ex), .en(1'b1), .clk(CLK), .Q(WA3_M));  // open: clr
  Register #(.width(2)) register_8 (.D(MUX_WB_Ex), .en(1'b1), .clk(CLK), .Q(MUX_WB_M));  // open: clr
  Register #(.width(3)) register_9 (.D(NZPEx), .en(1'b1), .clk(CLK), .Q(NZPM));  // open: clr
  Register #(.width(3)) register_10 (.D(ALUFEx), .en(1'b1), .clk(CLK), .Q(ALUFM));  // open: clr
  Register #(.width(1)) register_11 (.D(WEM_Ex), .en(1'b1), .clk(CLK), .Q(WEM_M));  // open: clr
  Register #(.width(1)) register_12 (.D(WER_Ex), .en(1'b1), .clk(CLK), .Q(WER_M));  // open: clr
endmodule

module WB_Register (
  input  [15:0] RD_M,
  input  [15:0] ALUResult_M,
  input  [2:0] WA3_M,
  input  [15:0] PCPlus_M,
  input  [1:0] MUX_WB_M,
  input  [3:0] OPCODE_M,
  input  WER_M,
  input  CLK,
  input  MUX_PC_M,
  output [15:0] RD_W,
  output [15:0] ALUResult_W,
  output [2:0] WA3_W,
  output [15:0] PCPlus_W,
  output [1:0] MUX_WB,
  output [3:0] OPCODE_W,
  output WER_WB,
  output MUX_PC_WB
);

  Register #(.width(16)) register_1 (.D(RD_M), .en(1'b1), .clk(CLK), .Q(RD_W));  // open: clr
  Register #(.width(16)) register_2 (.D(ALUResult_M), .en(1'b1), .clk(CLK), .Q(ALUResult_W));  // open: clr
  Register #(.width(16)) register_3 (.D(PCPlus_M), .en(1'b1), .clk(CLK), .Q(PCPlus_W));  // open: clr
  Register #(.width(4)) register_4 (.D(OPCODE_M), .en(1'b1), .clk(CLK), .Q(OPCODE_W));  // open: clr
  Register #(.width(1)) register_5 (.D(MUX_PC_M), .en(1'b1), .clk(CLK), .Q(MUX_PC_WB));  // open: clr
  Register #(.width(3)) register_6 (.D(WA3_M), .en(1'b1), .clk(CLK), .Q(WA3_W));  // open: clr
  Register #(.width(2)) register_7 (.D(MUX_WB_M), .en(1'b1), .clk(CLK), .Q(MUX_WB));  // open: clr
  Register #(.width(1)) register_8 (.D(WER_M), .en(1'b1), .clk(CLK), .Q(WER_WB));  // open: clr
endmodule

module DecoOPCODE (
  input  [3:0] OPCODE,
  output A1,
  output A2,
  output A3,
  output B1,
  output B2,
  output B3,
  output C1,
  output C2,
  output C3,
  output D1,
  output D2,
  output D3,
  output E1,
  output E2,
  output E3,
  output F1,
  output F2,
  output F3,
  output G1,
  output G2,
  output G3,
  output P1,
  output P2,
  output P3
);

  wire and_1_out, and_2_out, and_3_out, and_4_out, and_5_out, and_6_out, and_7_out, and_8_out, and_9_out,
       and_10_out, and_11_out, and_12_out, and_13_out, and_14_out, and_15_out, and_16_out, and_17_out,
       and_18_out, and_19_out, and_20_out, and_22_out, and_23_out, and_24_out, and_25_out, and_26_out,
       and_27_out, and_28_out, and_29_out, and_30_out, and_31_out, and_32_out, and_33_out, and_34_out,
       and_35_out, and_36_out, and_37_out, and_38_out, and_39_out, and_40_out, and_41_out, and_42_out,
       and_43_out, and_44_out, and_45_out, and_46_out, and_47_out, and_48_out, and_49_out, and_50_out,
       and_51_out, and_52_out, and_53_out, and_54_out, and_55_out, and_56_out, and_57_out, and_58_out,
       and_59_out, and_61_out, and_62_out, and_63_out, and_64_out, not_1_out, not_2_out, not_3_out, not_4_out;

  not not_1 (not_1_out, OPCODE[3]);
  not not_2 (not_2_out, OPCODE[2]);
  not not_3 (not_3_out, OPCODE[1]);
  not not_4 (not_4_out, OPCODE[0]);
  and and_1 (and_1_out, not_2_out, not_3_out, not_4_out);
  and and_2 (and_2_out, not_1_out, OPCODE[0]);
  and and_3 (and_3_out, not_2_out, OPCODE[1], OPCODE[0]);
  or or_1 (A2, not_1_out, not_2_out, not_4_out);
  and and_4 (and_4_out, not_2_out, not_3_out, OPCODE[0]);
  and and_5 (and_5_out, not_1_out, OPCODE[2]);
  and and_6 (and_6_out, OPCODE[2], not_4_out);
  and and_7 (and_7_out, not_1_out, OPCODE[0]);
  and and_8 (and_8_out, OPCODE[1], not_4_out);
  and and_9 (and_9_out, not_1_out, OPCODE[1], OPCODE[0]);
  and and_10 (and_10_out, not_2_out, OPCODE[1], OPCODE[0]);
  and and_11 (and_11_out, not_1_out, OPCODE[2], not_3_out, not_4_out);
  and and_12 (and_12_out, OPCODE[3], not_2_out, not_3_out, not_4_out);
  and and_13 (and_13_out, OPCODE[3], OPCODE[2], OPCODE[1], not_4_out);
  and and_14 (and_14_out, OPCODE[3], not_2_out, not_3_out, OPCODE[0]);
  and and_15 (and_15_out, OPCODE[3], OPCODE[2], not_4_out);
  and and_16 (and_16_out, not_2_out, not_3_out);
  and and_17 (and_17_out, not_1_out, OPCODE[0]);
  and and_18 (and_18_out, not_2_out, OPCODE[0]);
  and and_19 (and_19_out, not_1_out, OPCODE[2], not_3_out, not_4_out);
  and and_20 (and_20_out, OPCODE[3], OPCODE[2], OPCODE[1], not_4_out);
  and and_21 (C3, OPCODE[3], OPCODE[2], not_4_out);
  and and_22 (and_22_out, not_1_out, not_3_out);
  and and_23 (and_23_out, not_2_out, not_3_out);
  and and_24 (and_24_out, not_3_out, not_4_out);
  and and_25 (and_25_out, not_1_out, not_2_out, not_3_out, OPCODE[0]);
  and and_26 (and_26_out, not_1_out, OPCODE[1], not_4_out);
  and and_27 (and_27_out, not_2_out, OPCODE[1], not_4_out);
  and and_28 (and_28_out, not_1_out, not_3_out, OPCODE[0]);
  and and_29 (and_29_out, OPCODE[3], OPCODE[2], not_4_out);
  and and_30 (and_30_out, not_1_out, not_3_out);
  and and_31 (and_31_out, not_2_out, not_3_out);
  and and_32 (and_32_out, not_1_out, OPCODE[0]);
  and and_33 (and_33_out, not_1_out, OPCODE[1]);
  and and_34 (and_34_out, OPCODE[3], not_4_out);
  and and_35 (and_35_out, not_1_out, not_3_out, OPCODE[0]);
  and and_36 (and_36_out, not_1_out, OPCODE[2]);
  and and_37 (and_37_out, OPCODE[3], not_2_out);
  and and_38 (and_38_out, OPCODE[3], not_4_out);
  and and_39 (and_39_out, not_3_out, not_4_out);
  and and_40 (and_40_out, not_1_out, OPCODE[0]);
  and and_41 (and_41_out, not_2_out, OPCODE[0]);
  and and_42 (and_42_out, not_2_out, not_3_out, OPCODE[0]);
  and and_43 (and_43_out, not_2_out, OPCODE[1], not_4_out);
  and and_44 (and_44_out, not_1_out, OPCODE[2], not_3_out);
  and and_45 (and_45_out, not_1_out, OPCODE[2], not_4_out);
  and and_46 (and_46_out, OPCODE[2], not_3_out, not_4_out);
  and and_47 (and_47_out, not_1_out, not_3_out, OPCODE[0]);
  and and_48 (and_48_out, OPCODE[3], OPCODE[2], OPCODE[1], not_4_out);
  and and_49 (and_49_out, not_1_out, not_4_out);
  and and_50 (and_50_out, not_1_out, OPCODE[1]);
  and and_51 (and_51_out, not_2_out, OPCODE[1]);
  and and_52 (and_52_out, OPCODE[2], not_4_out);
  and and_53 (and_53_out, not_2_out, OPCODE[0]);
  and and_54 (and_54_out, not_1_out, OPCODE[1]);
  and and_55 (and_55_out, OPCODE[1], not_4_out);
  and and_56 (and_56_out, OPCODE[2], not_4_out);
  and and_57 (and_57_out, OPCODE[3], not_4_out);
  and and_58 (and_58_out, not_1_out, not_3_out, OPCODE[0]);
  and and_59 (and_59_out, not_2_out, not_3_out, OPCODE[0]);
  and and_60 (P1, OPCODE[3], OPCODE[2], OPCODE[0]);
  and and_61 (and_61_out, not_1_out, not_2_out, not_4_out);
  and and_62 (and_62_out, not_1_out, not_2_out, OPCODE[1]);
  and and_63 (and_63_out, OPCODE[3], OPCODE[2], OPCODE[0]);
  and and_64 (and_64_out, not_3_out, OPCODE[0]);
  or or_2 (A1, and_1_out, and_2_out, and_3_out);
  or or_3 (A3, and_4_out, and_5_out, and_6_out);
  or or_4 (B1, not_2_out, and_7_out, and_8_out);
  or or_5 (B2, and_9_out, and_10_out, and_11_out, and_12_out, and_13_out);
  or or_6 (B3, and_14_out, and_15_out);
  or or_7 (C1, and_16_out, and_17_out, and_18_out);
  or or_8 (C2, and_19_out, and_20_out);
  or or_9 (D1, and_22_out, and_23_out, and_24_out);
  or or_10 (D2, and_25_out, and_26_out, and_27_out);
  or or_11 (D3, and_28_out, and_29_out);
  or or_12 (E1, and_30_out, and_31_out, not_4_out);
  or or_13 (E2, not_2_out, and_32_out, and_33_out, and_34_out);
  or or_14 (E3, and_35_out, and_36_out, and_37_out, and_38_out);
  or or_15 (F1, and_39_out, and_40_out, and_41_out);
  or or_16 (F2, and_42_out, and_43_out, and_44_out, and_45_out, and_46_out);
  or or_17 (F3, and_47_out, and_48_out);
  or or_18 (G1, and_49_out, and_50_out, and_51_out, and_52_out);
  or or_19 (G2, and_53_out, and_54_out, and_55_out, and_56_out, and_57_out);
  or or_20 (G3, and_58_out, and_59_out);
  or or_21 (P2, and_61_out, and_62_out, and_63_out);
  or or_22 (P3, and_64_out, OPCODE[2], OPCODE[3]);
endmodule

module DataMemory (
  input  [15:0] A1,
  input  [15:0] A2,
  input  WE,
  input  [15:0] WD2,
  input  CLK,
  output [15:0] RD1
);

  wire not_1_out;
  wire [15:0] multiplexer_1_out;

  Multiplexer #(.width(16)) multiplexer_1 (.in0(A1), .in1(A2), .out(multiplexer_1_out), .sel(WE));
  RAM #(.addrWidth(16), .asyncread("true"), .dataWidth(16)) ram_1 (
    .addr(multiplexer_1_out), .we(WE), .oe(not_1_out), .clk(CLK), .din(WD2), .dout(RD1));
  not not_1 (not_1_out, WE);
endmodule

module InstructionMemory (
  input  [15:0] A,
  output [15:0] RD
);

  RAM #(.addrWidth(16), .asyncread("true"), .dataWidth(16)) ram_1 (.addr(A), .dout(RD));  // open: we, oe, clk, din
endmodule

module LogicaNZP (
  input  Salto_Cond,
  input  [2:0] INS_NZP,
  input  [2:0] ALU_NZP,
  output Salida
);

  wire and_1_out, and_2_out, and_3_out, or_1_out;

  and and_1 (and_1_out, INS_NZP[0], ALU_NZP[0]);
  and and_2 (and_2_out, INS_NZP[1], ALU_NZP[1]);
  and and_3 (and_3_out, INS_NZP[2], ALU_NZP[2]);
  or or_1 (or_1_out, and_1_out, and_2_out, and_3_out);
  and and_4 (Salida, Salto_Cond, or_1_out);
endmodule

module Hazard (
  input  [3:0] OP,
  input  bit5,
  input  [2:0] DR,
  input  [2:0] SR1,
  input  [2:0] SR2,
  output MUX_A_ALU,
  output MUX_B_ALU
);

  wire depende_1_sr, depende_1_sr1_baser, depende_1_sr2, nand_1_out, SR1_DR_i, SR2_DR_i;

  DEPENDE depende_1 (.op(OP), .SR(depende_1_sr), .SR1_BaseR(depende_1_sr1_baser), .SR2(depende_1_sr2));
  COMPARATOR_SRyDR SR1_DR (.SR1(SR1), .DR(DR), .i(SR1_DR_i));
  COMPARATOR_SRyDR SR2_DR (.SR1(SR2), .DR(DR), .i(SR2_DR_i));
  COMPARADOR_FW comparador_fw_1 ();  // open: RsE, RdM, WERM, Rd, WERW, SMux_ALU
  COMPARADOR_FW comparador_fw_2 ();  // open: RsE, RdM, WERM, Rd, WERW, SMux_ALU
  Multiplexer multiplexer_1 (.in0(1'b0), .in1(SR1_DR_i), .out(MUX_A_ALU), .sel(depende_1_sr1_baser));
  Multiplexer multiplexer_2 (.in0(SR2_DR_i), .in1(1'b0), .out(MUX_B_ALU), .sel(nand_1_out));
  nand nand_1 (nand_1_out, depende_1_sr2, bit5);
endmodule

module DEPENDE (
  input  [3:0] op,
  output SR,
  output SR1_BaseR,
  output SR2
);

  wire and_2_out, and_3_out, and_4_out, not_1_out, not_2_out, not_3_out, not_4_out;

  not not_1 (not_1_out, op[3]);
  not not_2 (not_2_out, op[2]);
  not not_3 (not_3_out, op[1]);
  not not_4 (not_4_out, op[0]);
  and and_1 (SR, op[1], op[0]);
  and and_2 (and_2_out, not_1_out, op[2]);
  and and_3 (and_3_out, not_2_out, not_3_out, op[0]);
  and and_4 (and_4_out, op[2], not_4_out);
  and and_5 (SR2, not_1_out, not_3_out, op[0]);
  or or_1 (SR1_BaseR, and_2_out, and_3_out, and_4_out);
endmodule

module COMPARATOR_SRyDR (
  input  [2:0] SR1,
  input  [2:0] DR,
  output i
);

  wire and_1_out, and_2_out, and_3_out, and_4_out, and_5_out, and_6_out, and_7_out, and_8_out, not_1_out,
       not_2_out, not_3_out, not_4_out, not_5_out, not_6_out;

  not not_1 (not_1_out, SR1[2]);
  not not_2 (not_2_out, SR1[1]);
  not not_3 (not_3_out, SR1[0]);
  not not_4 (not_4_out, DR[2]);
  not not_5 (not_5_out, DR[1]);
  not not_6 (not_6_out, DR[0]);
  and and_1 (and_1_out, not_1_out, not_2_out, not_3_out, not_4_out, not_5_out, not_6_out);
  and and_2 (and_2_out, not_1_out, SR1[1], not_3_out, not_4_out, DR[1], not_6_out);
  and and_3 (and_3_out, SR1[2], not_2_out, not_3_out, DR[2], not_5_out, not_6_out);
  and and_4 (and_4_out, SR1[2], SR1[1], not_3_out, DR[2], DR[1], not_6_out);
  and and_5 (and_5_out, not_1_out, not_2_out, SR1[0], not_4_out, not_5_out, DR[0]);
  and and_6 (and_6_out, not_1_out, SR1[1], SR1[0], not_4_out, DR[1], DR[0]);
  and and_7 (and_7_out, SR1[2], not_2_out, SR1[0], DR[2], not_5_out, DR[0]);
  and and_8 (and_8_out, SR1[2], SR1[1], SR1[0], DR[2], DR[1], DR[0]);
  or or_1 (i, and_1_out, and_2_out, and_3_out, and_4_out, and_5_out, and_6_out, and_7_out, and_8_out);
endmodule

module COMPARADOR_FW (
  input  [2:0] RsE,
  input  [2:0] RdM,
  input  WERM,
  input  [2:0] Rd,
  input  WERW,
  output [1:0] SMux_ALU
);

  wire not_1_out, not_2_out, not_3_out, not_4_out, not_5_out, not_6_out, not_7_out, not_8_out, not_9_out,
       or_1_out, or_2_out, or_3_out, or_4_out, or_5_out, or_6_out, or_7_out, or_8_out, or_9_out, or_10_out,
       or_11_out, or_12_out, or_13_out, or_14_out;

  not not_1 (not_1_out, RsE[2]);
  not not_2 (not_2_out, RsE[1]);
  not not_3 (not_3_out, RsE[0]);
  not not_4 (not_4_out, RdM[2]);
  not not_5 (not_5_out, RdM[1]);
  not not_6 (not_6_out, RdM[0]);
  not not_7 (not_7_out, Rd[2]);
  not not_8 (not_8_out, Rd[1]);
  not not_9 (not_9_out, Rd[0]);
  or or_1 (or_1_out, RsE[1], not_5_out);
  or or_2 (or_2_out, RsE[2], not_4_out);
  or or_3 (or_3_out, RsE[0], not_6_out);
  or or_4 (or_4_out, not_2_out, RdM[1]);
  or or_5 (or_5_out, not_3_out, RdM[0]);
  or or_6 (or_6_out, not_1_out, RdM[2]);
  or or_7 (or_7_out, RdM[2], RdM[1], RdM[0]);
  or or_8 (or_8_out, RsE[1], not_8_out);
  or or_9 (or_9_out, RsE[2], not_7_out);
  or or_10 (or_10_out, RsE[0], not_9_out);
  or or_11 (or_11_out, not_2_out, Rd[1]);
  or or_12 (or_12_out, not_3_out, Rd[0]);
  or or_13 (or_13_out, not_1_out, Rd[2]);
  or or_14 (or_14_out, Rd[2], Rd[1], Rd[0]);
  and and_1 (SMux_ALU[1], WERM, or_1_out, or_2_out, or_3_out, or_4_out, or_5_out, or_6_out, or_7_out);
  and and_2 (SMux_ALU[0], WERW, or_8_out, or_9_out, or_10_out, or_11_out, or_12_out, or_13_out, or_14_out);
endmodule
